# Fritzing sketch led_receiver (saved by Fritzing 0.9.1b)
breadboards: 1

parts:
  part = 2.4GHz Low Power Transceiver [package=qfn20]
  LED1 = LED - 5mm [color="Red (633nm)" package="5 mm [THT]"]
  R1 = Resistor [tolerance=±5% resistance=220 package=THT]
  part_2 = Arduino Pro Mini v13

nets:
  N1: part.CE, part_2.D7
  N2: part.CSN, part_2.D8
  N3: part.SCK, part_2.D13/SCK
  N4: part.MOSI, part_2.D11_PWM/MOSI
  N5: part.MISO, part_2.D12/MISO
  VDD: part.VDD, part_2.VCC
  VSS: part.VSS, LED1.cathode, part_2.GND
  N6: LED1.anode, R1.Pin_1
  N7: R1.Pin_0, part_2.D2
