# Fritzing sketch led_transmitter (saved by Fritzing 0.9.1b)
breadboards: 1

parts:
  part = 2.4GHz Low Power Transceiver [package=qfn20]
  part_2 = Arduino Pro Mini v13
  part_3 = Resistor [package="2512 [SMD]"]
  S1 = Pushbutton [package="[SMD]"]

nets:
  N1: part.CE, part_2.D7
  N2: part.CSN, part_2.D8
  N3: part.SCK, part_2.D13/SCK
  N4: part.MOSI, part_2.D11_PWM/MOSI
  N5: part.MISO, part_2.D12/MISO
  VDD: part.VDD, part_2.VCC, S1.Pin_2
  N6: part.VSS, part_3.Pin_0
  N7: part_2.D9_PWM, part_3.Pin_1, S1.Pin_3, S1.Pin_4
